# Fritzing sketch PullUp Configuration (saved by Fritzing 0.9.3b)
breadboards: 1

parts:
  Teensy_3_1 = Teensy 3.1  # not connected
  S1 = Momentary Switch [package=ksa_sealed_tac_switch]
  R1 = Resistor [tolerance=±5% resistance=220 package="0402 [SMD]"]

nets:
  N1: S1.3, R1.Pin_0

notes:
  Pull Up Configuration
  When the button is not pressed, the input pin is pulled 'high'.
  Dararancy San
  rancy.san@gmail.com
  https://rancy.dev
