# Fritzing sketch Push_Buttons_To_Control_LED_Colors (saved by Fritzing 0.9.3b)
breadboards: 1

parts:
  Teensy_3_1 = Teensy 3.1  # not connected
  R1 = Resistor [tolerance=±5% resistance=220 package="1206 [SMD]"]
  R2 = Resistor [tolerance=±5% resistance=220 package="1206 [SMD]"]
  R3 = Resistor [tolerance=±5% resistance=220 package="1206 [SMD]"]
  R4 = Resistor [tolerance=±1% resistance=10k package=THT]
  S1 = Pushbutton [package="[SMD]"]
  S2 = Pushbutton [package="[SMD]"]
  LED1 = RGB LED (com. cathode, rgb) [package="5 mm [THT]"]

nets:
  N1: R1.Pin_1, LED1.blue_anode
  N2: R2.Pin_1, LED1.common_cathode
  N3: R3.Pin_1, LED1.red_anode
  N4: R4.Pin_0, S1.Pin_3, S1.Pin_4
  N5: S1.Pin_1, S1.Pin_2, S2.Pin_1, S2.Pin_2, LED1.green_anode
  N6: S2.Pin_3, S2.Pin_4

notes:
  Pushbuttons to Control LED Colors
  Control a tricolor RGB with two switches and a pull-up resistor.
  Dararancy San
  rancy.san@gmail.com
  https://rancy.dev
