# Fritzing sketch 2 Shift Registers and 16 LEDs (saved by Fritzing 0.9.3b)
breadboards: 1

parts:
  Teensy_3_1 = Teensy 3.1  # not connected
  U1 = 74HC595 [package="DIP16 [THT]"]
  U2 = 74HC595 [package="DIP16 [THT]"]
  R1 = Resistor [tolerance=±5% resistance=220 package="2010 [SMD]"]
  R2 = Resistor [tolerance=±5% resistance=220 package="2010 [SMD]"]
  R3 = Resistor [tolerance=±5% resistance=220 package="2010 [SMD]"]
  R4 = Resistor [tolerance=±5% resistance=220 package="2010 [SMD]"]
  R5 = Resistor [tolerance=±5% resistance=220 package="2010 [SMD]"]
  R6 = Resistor [tolerance=±5% resistance=220 package="2010 [SMD]"]
  R7 = Resistor [tolerance=±5% resistance=220 package="2010 [SMD]"]
  R8 = Resistor [tolerance=±5% resistance=220 package="2010 [SMD]"]
  R9 = Resistor [tolerance=±5% resistance=220 package="2010 [SMD]"]
  R10 = Resistor [tolerance=±5% resistance=220 package="2010 [SMD]"]
  R11 = Resistor [tolerance=±5% resistance=220 package="2010 [SMD]"]
  R12 = Resistor [tolerance=±5% resistance=220 package="2010 [SMD]"]
  R13 = Resistor [tolerance=±5% resistance=220 package="2010 [SMD]"]
  R14 = Resistor [tolerance=±5% resistance=220 package="2010 [SMD]"]
  R15 = Resistor [tolerance=±5% resistance=220 package="2010 [SMD]"]
  R16 = Resistor [tolerance=±5% resistance=220 package="2010 [SMD]"]
  LED1 = smd LED [color="Red (633nm)" package="0805 [SMD]"]
  LED2 = smd LED [color="Red (633nm)" package="0805 [SMD]"]
  LED3 = smd LED [color="Red (633nm)" package="0805 [SMD]"]
  LED4 = smd LED [color="Red (633nm)" package="0805 [SMD]"]
  LED5 = smd LED [color="Red (633nm)" package="0805 [SMD]"]
  LED6 = smd LED [color="Red (633nm)" package="0805 [SMD]"]
  LED7 = smd LED [color="Red (633nm)" package="0805 [SMD]"]
  LED8 = smd LED [color="Red (633nm)" package="0805 [SMD]"]
  LED9 = smd LED [color="Yellow (595nm)" package="0603 [SMD]"]
  LED10 = smd LED [color="Yellow (595nm)" package="0603 [SMD]"]
  LED11 = smd LED [color="Yellow (595nm)" package="0603 [SMD]"]
  LED12 = smd LED [color="Yellow (595nm)" package="0603 [SMD]"]
  LED13 = smd LED [color="Green (565nm)" package="0603 [SMD]"]
  LED14 = smd LED [color="Green (565nm)" package="0603 [SMD]"]
  LED15 = smd LED [color="Green (565nm)" package="0603 [SMD]"]
  LED16 = smd LED [color="Green (565nm)" package="0603 [SMD]"]

nets:
  N1: U1.Q1, R2.Pin_1
  N2: U1.Q2, R3.Pin_1
  N3: U1.Q3, R4.Pin_1
  N4: U1.Q4, R5.Pin_1
  N5: U1.Q5, R6.Pin_1
  N6: U1.Q6, R8.Pin_1
  N7: U1.Q7, R7.Pin_1
  GND: U1.GND, U1.OE, U2.GND, U2.OE, LED1.cathode, LED2.cathode, LED3.cathode, LED4.cathode, LED5.cathode, LED6.cathode, LED7.cathode, LED8.cathode, LED9.cathode, LED10.cathode, LED11.cathode, LED12.cathode, LED13.cathode, LED14.cathode, LED15.cathode, LED16.cathode
  N8: U1.Q7', U2.DS
  VCC: U1.MR, U1.VCC, U2.MR, U2.VCC
  N9: U1.SH_CP, U2.SH_CP
  N10: U1.ST_CP, U2.ST_CP
  N11: U1.Q0, R1.Pin_1
  N12: U2.Q1, R15.Pin_1
  N13: U2.Q2, R11.Pin_1
  N14: U2.Q3, R12.Pin_1
  N15: U2.Q4, R9.Pin_1
  N16: U2.Q5, R14.Pin_1
  N17: U2.Q6, R13.Pin_1
  N18: U2.Q7, R10.Pin_1
  N19: U2.Q0, R16.Pin_1
  N20: R1.Pin_0, LED1.anode
  N21: R2.Pin_0, LED2.anode
  N22: R3.Pin_0, LED3.anode
  N23: R4.Pin_0, LED4.anode
  N24: R5.Pin_0, LED5.anode
  N25: R6.Pin_0, LED6.anode
  N26: R7.Pin_0, LED8.anode
  N27: R8.Pin_0, LED7.anode
  N28: R9.Pin_0, LED13.anode
  N29: R10.Pin_0, LED16.anode
  N30: R11.Pin_0, LED11.anode
  N31: R12.Pin_0, LED12.anode
  N32: R13.Pin_0, LED15.anode
  N33: R14.Pin_0, LED14.anode
  N34: R15.Pin_0, LED10.anode
  N35: R16.Pin_0, LED9.anode

notes:
  2 Shift Registers and 16 LEDs
  Control the illumination of the LEDs through the shift registers.
  Dararancy San
  rancy.san@gmail.com
  https://rancy.dev
