# Fritzing sketch BlinkwithLED (saved by Fritzing 0.9.3b)
breadboards: 1

parts:
  Teensy1 = Teensy 3.0  # not connected
  LED1 = LED - 5mm [color="Red (633nm)" package="5 mm [THT]"]
  R1 = Resistor [tolerance=±5% resistance=220 package=THT]

nets:
  N1: LED1.anode, R1.Pin_1

notes:
  Simple Blink
  Discrete red LED.
  Dararancy San
  rancy.san@gmail.com
  https://rancy.dev
